# Fritzing sketch MSGEQ7_Schematic (saved by Fritzing 0.8.7b)
breadboards: 1

parts:
  TRS2 = Audio Jack (TRS) 3.5mm [package="4Ucon 08780 [THT]"]
  Bauteil1 = Arduino Uno (Rev3)
  IC1 = IC, DIP package, 8 pins [chip_label=MSGEQ7L]
  IC2 = IC, DIP package, 8 pins [chip_label=MSGEQ7R]
  LED1 = LED - 5mm [color="Red (633nm)" package="5 mm [THT]"]
  C1 = Ceramic Capacitor [capacitance=100nF package="100 mil [THT, multilayer]"]
  C2 = Ceramic Capacitor [capacitance=100nF package="100 mil [THT, multilayer]"]
  C3 = Ceramic Capacitor [capacitance=33pF package="100 mil [THT, multilayer]"]
  C4 = Ceramic Capacitor [capacitance=33pF package="100 mil [THT, multilayer]"]
  R1 = Resistor [tolerance=±5% resistance=200k package=THT]
  R2 = Resistor [tolerance=±5% resistance=200k package=THT]
  C5 = Ceramic Capacitor [capacitance=100nF package="100 mil [THT, multilayer]"]
  C6 = Ceramic Capacitor [capacitance=100nF package="100 mil [THT, multilayer]"]
  C7 = Ceramic Capacitor [capacitance=10nF package="100 mil [THT, multilayer]"]
  C8 = Ceramic Capacitor [capacitance=10nF package="100 mil [THT, multilayer]"]
  R3 = Resistor [tolerance=±5% resistance=220 package=THT]

nets:
  N1: TRS2.Sleeve, Bauteil1.GND, IC1.pin2, IC2.pin2, C1.1, C2.1, C3.0, C4.0, C5.0, C6.0, R3.Pin_0
  N2: TRS2.Ring, C8.1
  N3: TRS2.Tip, C7.1
  N4: Bauteil1.A0, IC1.pin3
  N5: Bauteil1.A1, IC2.pin3
  N6: Bauteil1.A2, IC1.pin7, IC2.pin7
  N7: Bauteil1.A3, IC1.pin4, IC2.pin4
  N8: Bauteil1.D3_PWM, LED1.anode
  N9: Bauteil1.5V, IC1.pin1, IC2.pin1, C1.0, C2.0, R1.Pin_1, R2.Pin_1
  N10: IC1.pin5, C7.0
  N11: IC1.pin6, C6.1
  N12: IC1.pin8, C3.1, R2.Pin_0
  N13: IC2.pin5, C8.0
  N14: IC2.pin6, C5.1
  N15: IC2.pin8, C4.1, R1.Pin_0
  N16: LED1.cathode, R3.Pin_1

notes:
  Reset Pin A2
  Strobe Pin A3
  Left Pin A0
  Right Pin A1
  Led Pin 3 (PWM)
